# Fritzing sketch Color_Memory_Game_Schematic (saved by Fritzing 0.9.3b)
breadboards: 1

parts:
  Part1 = Arduino Uno (Rev3) - ICSP
  LED1 = LED - 5mm [color="Red (633nm)" package="5 mm [THT]"]
  LED2 = LED - 5mm [color="Blue (505nm)" package="5 mm [THT]"]
  LED3 = LED - 5mm [color="Yellow (574nm)" package="5 mm [THT]"]
  LED4 = LED - 5mm [color="Green (560nm)" package="5 mm [THT]"]
  S1 = Pushbutton [package="[SMD]"]
  S2 = Pushbutton [package="[SMD]"]
  S3 = Pushbutton [package="[SMD]"]
  S4 = Pushbutton [package="[SMD]"]
  SN74LS1 = SN74LS48 [package="DIP (Dual Inline) [THT]"]
  R1 = Resistor [tolerance=±5% resistance=1k package="0402 [SMD]"]
  R2 = Resistor [tolerance=±5% resistance=1k package="0402 [SMD]"]
  R3 = Resistor [tolerance=±5% resistance=1k package="0402 [SMD]"]
  R4 = Resistor [tolerance=±5% resistance=1k package="0402 [SMD]"]
  DI1 = 7-Segment LED Display [package=THT]
  R5 = Resistor [tolerance=±5% resistance=1k package="0402 [SMD]"]
  R6 = Resistor [tolerance=±5% resistance=1k package="0402 [SMD]"]

nets:
  N1: Part1.D8, LED3.anode
  N2: Part1.D9_PWM, LED4.anode
  N3: Part1.D10_PWM/SS, SN74LS1.A
  N4: Part1.D11_PWM/MOSI, SN74LS1.B
  N5: Part1.D12/MISO, SN74LS1.C
  N6: Part1.D13/SCK, SN74LS1.D
  N7: Part1.D2, S3.Pin_3, S3.Pin_4
  N8: Part1.D3_PWM, S2.Pin_3, S2.Pin_4
  N9: Part1.D4, S1.Pin_3, S1.Pin_4
  N10: Part1.D5_PWM, S4.Pin_3, S4.Pin_4
  N11: Part1.D6_PWM, LED1.anode
  N12: Part1.D7, LED2.anode
  5V: Part1.5V, SN74LS1.LT, SN74LS1.BI/RBO, SN74LS1.VCC, R6.Pin_0
  GND: Part1.GND, S1.Pin_1, S1.Pin_2, S2.Pin_1, S2.Pin_2, S3.Pin_1, S3.Pin_2, S4.Pin_1, S4.Pin_2, SN74LS1.RBI, SN74LS1.GND, R1.Pin_1, R2.Pin_1, R3.Pin_1, R4.Pin_1, DI1.cathodeDP, R5.Pin_1
  N13: LED1.cathode, R1.Pin_0
  N14: LED2.cathode, R2.Pin_0
  N15: LED3.cathode, R3.Pin_0
  N16: LED4.cathode, R4.Pin_0
  N17: SN74LS1.e, DI1.cathodeE
  N18: SN74LS1.d, DI1.cathodeD
  N19: SN74LS1.c, DI1.cathodeC
  N20: SN74LS1.b, DI1.cathodeB
  N21: SN74LS1.a, DI1.cathodeA
  N22: SN74LS1.g, DI1.cathodeG
  N23: SN74LS1.f, DI1.cathodeF
  N24: DI1.commAnode#2, R5.Pin_0
  N25: DI1.commAnode#7, R6.Pin_1

custom parts:
  SN74LS48: BCD-TO-SEVEN-SEGMENT DECODERS/DRIVERS
